# Fritzing sketch navidad_mqtt (saved by Fritzing 0.9.3b)
breadboards: 2

parts:
  U1 = NodeMCU V1.0
  J1 = Piezo Speaker
  R1 = Resistor [tolerance=±5% resistance=220 package=THT]
  R2 = Resistor [tolerance=±5% resistance=220 package=THT]
  LED2 = LED - 5mm [color="Red (633nm)" package="5 mm [THT]"]
  Q2 = PNP-Transistor [package="TO92 [THT]"]
  LED3 = LED - 5mm [color="Red (633nm)" package="5 mm [THT]"]
  Q3 = NPN-Transistor [package="TO92 [THT]"]
  S1 = Pushbutton [package="[THT]"]
  S2 = Pushbutton [package="[THT]"]
  R3 = Resistor [tolerance=±5% resistance=10k package=THT]
  R4 = Resistor [tolerance=±5% resistance=10k package=THT]
  R5 = Resistor [tolerance=±5% resistance=220 package=THT]

nets:
  N1: U1.D1, Q2.C
  N2: U1.D2, S2.Pin_1, S2.Pin_2, R4.Pin_0
  N3: U1.D3, S1.Pin_1, S1.Pin_2, R3.Pin_0
  N4: U1.3V3, R1.Pin_1, R2.Pin_1, S1.Pin_3, S1.Pin_4, S2.Pin_3, S2.Pin_4
  N5: U1.GND, J1.pin1, R3.Pin_1, R4.Pin_1
  N6: U1.D7, Q3.C
  N7: U1.D8, Q2.B, Q3.B, R5.Pin_0
  N8: J1.pin2, R5.Pin_1
  N9: R1.Pin_0, LED3.anode
  N10: R2.Pin_0, LED2.anode
  N11: LED2.cathode, Q2.E
  N12: LED3.cathode, Q3.E

custom parts:
  NodeMCU V1.0: ESP8266 based NodeMCU
